// Logisim project logisim.circ as structural Verilog: 9 circuits, main circuit main
module main (
  input  [7:0] in_1,
  input  [7:0] in_2,
  input  [7:0] in_3,
  input  in_4,
  input  in_5
);

  wire AI, alu_1_c_flag, alu_1_n_flag, alu_1_z_flag, and_1_out, and_2_out, and_3_out, AO, BI, BO, CLK,
       clock_1_out, EC, EO, ES, FF, FI, II, MC, MHI, MLI, MTP, MZ, not_1_out, PCC, PHI, PLI, Reset, RI, RO,
       XE, XI, XO;
  wire [3:0] flags_1_flags_out;
  wire [7:0] DerBus, ir_1_instruction, multiplexer_1_out, multiplexer_2_out, multiplexer_3_out,
       multiplexer_4_out, registers_1_a_out, registers_1_b_out, registers_1_x_out, rom_1_data;
  wire [14:0] mar_1_addr_out;
  wire [15:0] pc_1_addr_out;
  wire [15:15] mar_1_addr_out_2;

  and and_1 (and_1_out, RI, mar_1_addr_out_2[15]);
  and and_2 (and_2_out, mar_1_addr_out_2[15], RO);
  ROM #(.addrWidth(15)) rom_1 (.addr(mar_1_addr_out), .data(rom_1_data));
  RAM #(.addrWidth(15), .databus("bidir"), .trigger("falling")) ram_1 (
    .addr(mar_1_addr_out), .we(and_1_out), .oe(and_2_out), .clk(CLK), .data(DerBus));
  PC pc_1 (
    .Reset(Reset), .PLI(PLI), .PCC(PCC), .CLK(CLK), .PHI(PHI), .L_Addr_In(DerBus), .H_Addr_In(DerBus),
    .Addr_Out(pc_1_addr_out));
  Multiplexer #(.width(8)) multiplexer_1 (.in0(DerBus), .in1(pc_1_addr_out[7:0]), .out(multiplexer_1_out), .sel(MTP));
  MAR mar_1 (
    .Reset(Reset), .MLI(MLI), .MC(MC), .CLK(CLK), .MHI(MHI), .L_Addr_In(multiplexer_1_out),
    .H_Addr_In(multiplexer_2_out), .Addr_Out({mar_1_addr_out_2[15], mar_1_addr_out}));
  Multiplexer #(.width(8)) multiplexer_2 (
    .in0(multiplexer_3_out), .in1(pc_1_addr_out[15:8]), .out(multiplexer_2_out), .sel(MTP));
  assign DerBus = and_3_out ? rom_1_data : 8'bz;  // Controlled_Buffer controlled_buffer_1
  and and_3 (and_3_out, not_1_out, RO);
  not not_1 (not_1_out, mar_1_addr_out_2[15]);
  Multiplexer #(.width(8)) multiplexer_3 (.in0(DerBus), .in1(in_2), .out(multiplexer_3_out), .sel(MZ));
  assign DerBus = FF ? in_1 : 8'bz;  // Controlled_Buffer controlled_buffer_2
  Registers registers_1 (
    .Reset(Reset), .A_In(AI), .X_In(XI), .B_in(BI), .CLK(CLK), .Bus_In(DerBus), .A_Out(registers_1_a_out),
    .X_Out(registers_1_x_out), .B_Out(registers_1_b_out));
  Multiplexer #(.width(8)) multiplexer_4 (
    .in0(registers_1_a_out), .in1(registers_1_x_out), .out(multiplexer_4_out), .sel(XE));
  ALU alu_1 (
    .EO(EO), .EC(EC), .ES(ES), .A(multiplexer_4_out), .B(registers_1_b_out), .Bus_Out(DerBus),
    .C_Flag(alu_1_c_flag), .Z_Flag(alu_1_z_flag), .N_Flag(alu_1_n_flag));
  Flags flags_1 (
    .Carry(alu_1_c_flag), .Zero(alu_1_z_flag), .Negative(alu_1_n_flag), .Bonus(1'b0), .FI(FI), .Reset(Reset),
    .CLK(CLK), .Flags_Out(flags_1_flags_out));
  IR ir_1 (.Reset(Reset), .Bus_In(DerBus), .II(II), .CLK(CLK), .Instruction(ir_1_instruction));
  Control control_1 (
    .Instruction(ir_1_instruction), .Flags_In(flags_1_flags_out), .Reset(Reset), .CLK(CLK),
    .Control_Word({FF, PCC, PHI, PLI, MZ, MTP, MC, MHI, MLI, RI, RO, FI, II, BI, XI, AI, BO, XO, AO, ES, EC, EO, XE}));
  assign DerBus = XO ? registers_1_x_out : 8'bz;  // Controlled_Buffer controlled_buffer_3
  assign DerBus = BO ? registers_1_b_out : 8'bz;  // Controlled_Buffer controlled_buffer_4
  Clock clock_1 (.out(clock_1_out));
  Button button_1 (.out(Reset));
  assign DerBus = AO ? registers_1_a_out : 8'bz;  // Controlled_Buffer controlled_buffer_5
  and and_4 (CLK, clock_1_out, ~in_5);  // AND_Gate
  // Probe on DerBus
  assign DerBus = in_4 ? in_3 : 8'bz;  // Controlled_Buffer controlled_buffer_6

  // Notes on the sheet:
  //   in_2: initial=0x80
  //   in_1: initial=0xff
  //   contents of rom_1 (hex, n*v repeats v):
  //   1 1 2 0 3 1 4 0 5
endmodule

module ALU (
  input  EO,
  input  EC,
  input  ES,
  input  [7:0] A,
  input  [7:0] B,
  output [7:0] Bus_Out,
  output C_Flag,
  output Z_Flag,
  output N_Flag
);

  wire and_2_out, and_3_out, and_4_out, not_1_out, not_2_out;
  wire [6:0] adder_1_out;
  wire [7:0] and_1_out, bit_extender_1_out, or_1_out, xor_1_out, xor_2_out;

  assign bit_extender_1_out = {{7{ES}}, ES};  // Bit_Extender bit_extender_1
  not not_1 (not_1_out, EO);
  assign xor_1_out = bit_extender_1_out ^ B;  // XOR_Gate xor_1, 8 bits wide
  assign or_1_out = B | A;  // OR_Gate or_1, 8 bits wide
  assign and_1_out = B & A;  // AND_Gate and_1, 8 bits wide
  assign xor_2_out = B ^ A;  // XOR_Gate xor_2, 8 bits wide
  and and_2 (and_2_out, ES, EC, not_1_out);
  Adder adder_1 (.a(A), .b(xor_1_out), .out({N_Flag, adder_1_out}), .cin(EC), .cout(C_Flag));
  assign Bus_Out = and_3_out ? and_1_out : 8'bz;  // Controlled_Buffer controlled_buffer_1
  assign Bus_Out = and_2_out ? xor_2_out : 8'bz;  // Controlled_Buffer controlled_buffer_2
  not not_2 (not_2_out, and_2_out);
  and and_3 (and_3_out, not_1_out, not_2_out, EC);
  and and_4 (and_4_out, not_1_out, not_2_out, ES);
  assign Bus_Out = EO ? {N_Flag, adder_1_out} : 8'bz;  // Controlled_Buffer controlled_buffer_3
  assign Bus_Out = and_4_out ? or_1_out : 8'bz;  // Controlled_Buffer controlled_buffer_4
  nor nor_1 (Z_Flag, adder_1_out[0], adder_1_out[1], adder_1_out[2], adder_1_out[3], adder_1_out[4], adder_1_out[5], adder_1_out[6], N_Flag);
endmodule

module Registers (
  input  Reset,
  input  [7:0] Bus_In,
  input  A_In,
  input  X_In,
  input  B_in,
  input  CLK,
  output [7:0] A_Out,
  output [7:0] X_Out,
  output [7:0] B_Out
);

  Register register_1 (.D(Bus_In), .en(A_In), .clk(CLK), .Q(A_Out), .clr(Reset));
  Register register_2 (.D(Bus_In), .en(X_In), .clk(CLK), .Q(X_Out), .clr(Reset));
  Register register_3 (.D(Bus_In), .en(B_in), .clk(CLK), .Q(B_Out), .clr(Reset));
endmodule

module MAR (
  input  Reset,
  input  MLI,
  input  MC,
  input  CLK,
  input  [7:0] L_Addr_In,
  input  MHI,
  input  [7:0] H_Addr_In,
  output [15:0] Addr_Out
);

  wire counter_1_carry;

  Counter counter_1 (
    .clr(Reset), .load(MLI), .up(1'b1), .count(MC), .clk(CLK), .D(L_Addr_In), .carry(counter_1_carry),
    .Q(Addr_Out[7:0]));
  Counter counter_2 (
    .clr(Reset), .load(MHI), .up(1'b1), .count(counter_1_carry), .clk(CLK), .D(H_Addr_In), .Q(Addr_Out[15:8]));  // open: carry

  // Notes on the sheet:
  //   LMR
  //   HMR
endmodule

module PC (
  input  Reset,
  input  PLI,
  input  PCC,
  input  CLK,
  input  [7:0] L_Addr_In,
  input  PHI,
  input  [7:0] H_Addr_In,
  output [15:0] Addr_Out
);

  wire counter_1_carry;

  Counter counter_1 (
    .clr(Reset), .load(PLI), .up(1'b1), .count(PCC), .clk(CLK), .D(L_Addr_In), .carry(counter_1_carry),
    .Q(Addr_Out[7:0]));
  Counter counter_2 (
    .clr(Reset), .load(PHI), .up(1'b1), .count(counter_1_carry), .clk(CLK), .D(H_Addr_In), .Q(Addr_Out[15:8]));  // open: carry

  // Notes on the sheet:
  //   LPC
  //   HPC
endmodule

module Flags (
  input  Carry,
  input  Zero,
  input  Negative,
  input  Bonus,
  input  FI,
  input  Reset,
  input  CLK,
  output [3:0] Flags_Out
);

  Register #(.width(4)) register_1 (.D({Bonus, Negative, Zero, Carry}), .en(FI), .clk(CLK), .Q(Flags_Out), .clr(Reset));
  LED led_1 (.in(Flags_Out[0]));
  LED led_2 (.in(Flags_Out[1]));
  LED led_3 (.in(Flags_Out[2]));
  LED led_4 (.in(Flags_Out[3]));
endmodule

module Serial (
  input  [7:0] Bus_In,
  output RDY_Flag
);


  assign RDY_Flag = 1'b0;
endmodule

module Control (
  input  [7:0] Instruction,
  input  [3:0] Flags_In,
  input  Reset,
  input  CLK,
  output [22:0] Control_Word
);

  wire Reset_Counter;
  wire [3:0] counter_1_q;

  ROM #(.addrWidth(16), .dataWidth(24)) rom_1 (
    .addr({Instruction, Flags_In, counter_1_q}), .data({Reset_Counter, Control_Word}));
  Counter #(.max('hf), .width(4)) counter_1 (
    .clr(Reset), .load(Reset_Counter), .up(1'b1), .count(1'b1), .clk(CLK), .Q(counter_1_q));  // open: D, carry

  // Notes on the sheet:
  //   contents of rom_1 (hex, n*v repeats v):
  //   211400 15*400000 211400 15*400000 211400 15*400000 211400 15*400000 211400 15*400000 211400
  //   15*400000 211400 15*400000 211400 15*400000 211400 15*400000 211400 15*400000 211400 15*400000
  //   211400 15*400000 211400 15*400000 211400 15*400000 211400 15*400000 211400 15*400000 211400 211200
  //   800882 13*0 211400 211200 800882 13*0 211400 211200 800882 13*0 211400 211200 800882 13*0 211400
  //   211200 800882 13*0 211400 211200 800882 13*0 211400 211200 800882 13*0 211400 211200 800882 13*0
  //   211400 211200 800882 13*0 211400 211200 800882 13*0 211400 211200 800882 13*0 211400 211200 800882
  //   13*0 211400 211200 800882 13*0 211400 211200 800882 13*0 211400 211200 800882 13*0 211400 211200
  //   800882 13*0 211400 24d000 1200 82c882 12*0 211400 24d000 1200 82c882 12*0 211400 24d000 1200 82c882
  //   12*0 211400 24d000 1200 82c882 12*0 211400 24d000 1200 82c882 12*0 211400 24d000 1200 82c882 12*0
  //   211400 24d000 1200 82c882 12*0 211400 24d000 1200 82c882 12*0 211400 24d000 1200 82c882 12*0 211400
  //   24d000 1200 82c882 12*0 211400 24d000 1200 82c882 12*0 211400 24d000 1200 82c882 12*0 211400 24d000
  //   1200 82c882 12*0 211400 24d000 1200 82c882 12*0 211400 24d000 1200 82c882 12*0 211400 24d000 1200
  //   82c882 12*0 211400 211200 80088e 13*0 211400 211200 80088e 13*0 211400 211200 80088e 13*0 211400
  //   211200 80088e 13*0 211400 211200 80088e 13*0 211400 211200 80088e 13*0 211400 211200 80088e 13*0
  //   211400 211200 80088e 13*0 211400 211200 80088e 13*0 211400 211200 80088e 13*0 211400 211200 80088e
  //   13*0 211400 211200 80088e 13*0 211400 211200 80088e 13*0 211400 211200 80088e 13*0 211400 211200
  //   80088e 13*0 211400 211200 80088e 13*0 211400 24d000 1200 82c88e 12*0 211400 24d000 1200 82c88e 12*0
  //   211400 24d000 1200 82c88e 12*0 211400 24d000 1200 82c88e 12*0 211400 24d000 1200 82c88e 12*0 211400
  //   24d000 1200 82c88e 12*0 211400 24d000 1200 82c88e 12*0 211400 24d000 1200 82c88e 12*0 211400 24d000
  //   1200 82c88e 12*0 211400 24d000 1200 82c88e 12*0 211400 24d000 1200 82c88e 12*0 211400 24d000 1200
  //   82c88e 12*0 211400 24d000 1200 82c88e 12*0 211400 24d000 1200 82c88e 12*0 211400 24d000 1200 82c88e
  //   12*0 211400 24d000 1200 82c88e 12*0 211400 91000 101000 c2c000 12*0 211400 91000 101000 c2c000 12*0
  //   211400 e10000 14*0 211400 e10000 14*0 211400 91000 101000 c2c000 12*0 211400 91000 101000 c2c000
  //   12*0 211400 e10000 14*0 211400 e10000 14*0 211400 91000 101000 c2c000 12*0 211400 91000 101000
  //   c2c000 12*0 211400 e10000 14*0 211400 e10000 14*0 211400 91000 101000 c2c000 12*0 211400 91000
  //   101000 c2c000 12*0 211400 e10000 14*0 211400 e10000
endmodule

module IR (
  input  Reset,
  input  [7:0] Bus_In,
  input  II,
  input  CLK,
  output [7:0] Instruction
);

  Register register_1 (.D(Bus_In), .en(II), .clk(CLK), .Q(Instruction), .clr(Reset));
endmodule
