// Logisim project 64x4.circ as structural Verilog
module PC (
  input  [7:0] in_1
);

  wire [7:0] controlled_buffer_1_out;

  Controlled_Buffer #(.width(8)) controlled_buffer_1 (.in(in_1), .out(controlled_buffer_1_out));  // open: en

  // Notes on the sheet:
  //   in_1: initial=0xff
  //   74HC245 (Octal Bus Transceiver)
endmodule
