// Logisim project SAP_1.circ as structural Verilog: 10 circuits, main circuit main
module main (
);

  wire and_1_out, bcd_to_7_segment_decoder_1_p1, bcd_to_7_segment_decoder_1_p2, button_2_out, CLK,
       clock_1_out, CLR, Cp, Ea, Ei, Ep, Er, Eu, HLT, La, Lb, Li, Lm, Lo, Lp, Lr, Su;
  wire [3:0] CTRL, Mem_Addr;
  wire [7:0] accumulator_1_alu_out, b_reg_1_alu_out, binary_to_bcd_converter_1_p1, W_Bus;

  RAM #(.addrWidth(4), .databus("bidir"), .trigger("high")) ram_1 (.addr(Mem_Addr), .we(Lr), .oe(Er), .data(W_Bus));
  Program_Counter program_counter_1 (
    .CLR(CLR), .Lp(Lp), .Cp(Cp), .CLK(CLK), .Addr_In(W_Bus), .Ep(Ep), .Addr_Out(W_Bus));
  Input_MAR input_mar_1 (.Lm(Lm), .CLK(CLK), .CLR(CLR), .Addr_In(W_Bus), .Addr_Out(Mem_Addr));
  Instruction_Reg instruction_reg_1 (
    .Li(Li), .CLK(CLK), .CLR(CLR), .Ei(Ei), .Bus_In(W_Bus), .Control_Out(CTRL), .Bus_Out(W_Bus));
  Controller controller_1 (
    .Instruction(CTRL), .CLK(CLK), .CLR(CLR), .HLT(HLT), .Eu(Lo), .Lb(Su), .Lo(Eu), .Cp(Cp), .Ep(Ep),
    .Lp(Lp), .Lm(Lm), .Lr(Lr), .Er(Er), .Li(Li), .Ei(Ei), .La(La), .Ea(Ea), .Su(Lb));
  Button button_1 (.out(CLR));
  Button button_2 (.out(button_2_out));
  Clock clock_1 (.out(clock_1_out));
  _7_Segment_Display u_7_segment_display_1 ();  // open: g, f, a, b, e, d, c, dp
  // BCD_to_7_Segment_decoder bcd_to_7_segment_decoder_1: pin names not known; wires that end beside it: bcd_to_7_segment_decoder_1_p1, bcd_to_7_segment_decoder_1_p2
  // Binary_to_BCD_converter #(.binvalue(8)) binary_to_bcd_converter_1: pin names not known; wires that end beside it: binary_to_bcd_converter_1_p1
  and and_1 (and_1_out, ~HLT, clock_1_out);  // AND_Gate
  _7_Segment_Display u_7_segment_display_2 ();  // open: g, f, a, b, e, d, c, dp
  _7_Segment_Display u_7_segment_display_3 ();  // open: g, f, a, b, e, d, c, dp
  // BCD_to_7_Segment_decoder bcd_to_7_segment_decoder_2: pin names not known
  // BCD_to_7_Segment_decoder bcd_to_7_segment_decoder_3: pin names not known
  or or_1 (CLK, button_2_out, and_1_out);
  Accumulator accumulator_1 (
    .La(La), .CLK(CLK), .Ea(Ea), .CLR(CLR), .Bus_In(W_Bus), .ALU_Out(accumulator_1_alu_out), .Bus_Out(W_Bus));
  ALU alu_1 (.Su(Su), .Eu(Eu), .A_In(accumulator_1_alu_out), .B_In(b_reg_1_alu_out), .Bus_Out(W_Bus));
  B_Reg b_reg_1 (.Bus_In(W_Bus), .Lb(Lb), .CLK(CLK), .CLR(CLR), .ALU_Out(b_reg_1_alu_out));
  Output_Reg output_reg_1 (.Lo(Lo), .CLK(CLK), .CLR(CLR), .Bus_In(W_Bus), .LED_Out(binary_to_bcd_converter_1_p1));

  // Notes on the sheet:
  //   Reset
  //   Single Step
endmodule

module Program_Counter (
  input  CLR,
  input  Lp,
  input  Cp,
  input  CLK,
  input  [7:0] Addr_In,
  input  Ep,
  output [7:0] Addr_Out
);

  wire [3:0] bit_extender_1_out, counter_1_q;
  wire [7:0] bit_extender_2_out;

  Bit_Extender #(.out_width(4), .\type ("zero")) bit_extender_1 (.in(Addr_In), .out(bit_extender_1_out));
  Counter #(.max('hf), .width(4)) counter_1 (
    .clr(CLR), .load(Lp), .up(1'b1), .count(Cp), .clk(CLK), .D(bit_extender_1_out), .Q(counter_1_q));  // open: carry
  Hex_Digit_Display hex_digit_display_1 (.value(counter_1_q));  // open: dp
  assign bit_extender_2_out = {{4{1'b0}}, counter_1_q};  // Bit_Extender bit_extender_2
  assign Addr_Out = Ep ? bit_extender_2_out : 8'bz;  // Controlled_Buffer controlled_buffer_1
endmodule

module Instruction_Reg (
  input  [7:0] Bus_In,
  input  Li,
  input  CLK,
  input  CLR,
  input  Ei,
  output [3:0] Control_Out,
  output [7:0] Bus_Out
);

  wire [3:0] register_1_q;
  wire [7:0] bit_extender_1_out;

  Register register_1 (.D(Bus_In), .en(Li), .clk(CLK), .Q({Control_Out, register_1_q}), .clr(CLR));
  Hex_Digit_Display hex_digit_display_1 (.value(register_1_q));  // open: dp
  Hex_Digit_Display hex_digit_display_2 (.value(Control_Out));  // open: dp
  assign bit_extender_1_out = {{4{1'b0}}, register_1_q};  // Bit_Extender bit_extender_1
  assign Bus_Out = Ei ? bit_extender_1_out : 8'bz;  // Controlled_Buffer controlled_buffer_1
endmodule

module Input_MAR (
  input  [7:0] Addr_In,
  input  Lm,
  input  CLK,
  input  CLR,
  output [3:0] Addr_Out
);

  wire [3:0] bit_extender_1_out;

  Bit_Extender #(.out_width(4), .\type ("zero")) bit_extender_1 (.in(Addr_In), .out(bit_extender_1_out));
  Register #(.width(4)) register_1 (.D(bit_extender_1_out), .en(Lm), .clk(CLK), .Q(Addr_Out), .clr(CLR));
  Hex_Digit_Display hex_digit_display_1 (.value(Addr_Out));  // open: dp
endmodule

module Accumulator (
  input  [7:0] Bus_In,
  input  La,
  input  CLK,
  input  Ea,
  input  CLR,
  output [7:0] ALU_Out,
  output [7:0] Bus_Out
);

  Register register_1 (.D(Bus_In), .en(La), .clk(CLK), .Q(ALU_Out), .clr(CLR));
  assign Bus_Out = Ea ? ALU_Out : 8'bz;  // Controlled_Buffer controlled_buffer_1
endmodule

module B_Reg (
  input  [7:0] Bus_In,
  input  Lb,
  input  CLK,
  input  CLR,
  output [7:0] ALU_Out
);

  Register register_1 (.D(Bus_In), .en(Lb), .clk(CLK), .Q(ALU_Out), .clr(CLR));
endmodule

module Output_Reg (
  input  [7:0] Bus_In,
  input  Lo,
  input  CLK,
  input  CLR,
  output [7:0] LED_Out
);

  Register register_1 (.D(Bus_In), .en(Lo), .clk(CLK), .Q(LED_Out), .clr(CLR));
endmodule

module ALU (
  input  Su,
  input  [7:0] A_In,
  input  [7:0] B_In,
  input  Eu,
  output [7:0] Bus_Out
);

  wire [7:0] adder_1_out, bit_extender_1_out, xor_1_out;

  assign bit_extender_1_out = {{7{Su}}, Su};  // Bit_Extender bit_extender_1
  assign xor_1_out = bit_extender_1_out ^ B_In;  // XOR_Gate xor_1, 8 bits wide
  Adder adder_1 (.a(A_In), .b(xor_1_out), .out(adder_1_out), .cin(Su));  // open: cout
  Hex_Digit_Display hex_digit_display_1 (.value(adder_1_out[7:4]));  // open: dp
  Hex_Digit_Display hex_digit_display_2 (.value(adder_1_out[3:0]));  // open: dp
  assign Bus_Out = Eu ? adder_1_out : 8'bz;  // Controlled_Buffer controlled_buffer_1
endmodule

module Addder (
  input  A,
  input  B,
  input  Ci,
  output Y,
  output Co
);

  wire and_1_out, and_2_out, xor_1_out;

  and and_1 (and_1_out, A, B);
  xor xor_1 (xor_1_out, A, B);
  and and_2 (and_2_out, xor_1_out, Ci);
  xor xor_2 (Y, xor_1_out, Ci);
  or or_1 (Co, and_1_out, and_2_out);
endmodule

module Controller (
  input  [3:0] Instruction,
  input  CLK,
  input  CLR,
  output HLT,
  output Cp,
  output Ep,
  output Lp,
  output Lm,
  output Lr,
  output Er,
  output Li,
  output Ei,
  output La,
  output Ea,
  output Su,
  output Eu,
  output Lb,
  output Lo
);

  wire and_2_out, and_3_out, j_k_ff_1_q, j_k_ff_1_qn, j_k_ff_2_q, j_k_ff_2_qn, j_k_ff_3_q, j_k_ff_3_qn,
       j_k_ff_4_q, j_k_ff_4_qn, j_k_ff_5_q, j_k_ff_5_qn, not_1_out, not_2_out, not_3_out, or_1_out, or_2_out;
  wire [5:0] counter_1_q, rom_1_data;

  or or_1 (or_1_out, CLR, and_3_out);
  not not_1 (not_1_out, CLK);
  J_K_Flip_Flop j_k_ff_1 (
    .J(j_k_ff_5_qn), .K(j_k_ff_5_q), .clk(not_1_out), .Q(j_k_ff_1_q), .Qn(j_k_ff_1_qn), .reset(or_1_out));  // open: preset
  J_K_Flip_Flop j_k_ff_2 (
    .J(j_k_ff_1_qn), .K(j_k_ff_1_q), .clk(not_1_out), .Q(j_k_ff_2_q), .Qn(j_k_ff_2_qn), .reset(or_1_out));  // open: preset
  J_K_Flip_Flop j_k_ff_3 (
    .J(j_k_ff_2_q), .K(j_k_ff_2_qn), .clk(not_1_out), .Q(j_k_ff_3_q), .Qn(j_k_ff_3_qn), .reset(or_1_out));  // open: preset
  J_K_Flip_Flop j_k_ff_4 (
    .J(j_k_ff_3_q), .K(j_k_ff_3_qn), .Q(j_k_ff_4_q), .Qn(j_k_ff_4_qn), .reset(or_1_out));  // open: clk, preset
  J_K_Flip_Flop j_k_ff_5 (
    .J(j_k_ff_4_q), .K(j_k_ff_4_qn), .clk(not_1_out), .Q(j_k_ff_5_q), .Qn(j_k_ff_5_qn), .reset(or_1_out));  // open: preset
  and and_1 (HLT, Instruction[0], Instruction[1], Instruction[2], Instruction[3]);
  or or_2 (or_2_out, or_1_out, j_k_ff_1_qn);
  not not_2 (not_2_out, or_2_out);
  not not_3 (not_3_out, CLK);
  ROM #(.addrWidth(4), .dataWidth(6)) rom_1 (.addr(Instruction), .data(rom_1_data));
  and and_2 (and_2_out, or_2_out, not_2_out);
  Counter #(.max('h3f), .width(6)) counter_1 (
    .clr(and_2_out), .load(j_k_ff_2_q), .up(1'b1), .count(1'b1), .clk(not_3_out), .D(rom_1_data),
    .Q(counter_1_q));  // open: carry
  ROM #(.addrWidth(6), .dataWidth(14)) rom_2 (
    .addr(counter_1_q), .data({Lo, Lb, Eu, Su, Ea, La, Ei, Li, Er, Lr, Lm, Lp, Ep, Cp}));
  and and_3 (and_3_out, ~Cp, Ep, ~Lp, ~Lm, ~Lr, Er, ~Li, Ei, ~La, Ea, ~Su, Eu, ~Lb, ~Lo);  // AND_Gate

  // Notes on the sheet:
  //   Ring Counter
  //   Rising Edge Detection
  //   contents of rom_1 (hex, n*v repeats v):
  //   2 4 6 8 a d 10 13 16 19 1c 1e 20 0 23 25
  //   contents of rom_2 (hex, n*v repeats v):
  //   a 61 2100 aa2 3100 aa2 180 aa2 480 aa2 88 120 aa2 88 420 aa2 480 2100 aa2 480 3100 aa2 88 420 2100
  //   88 420 3100 a00 aa2 600 aa2 88 210 aa2 84 aa2 0 aa2
endmodule
